// Logisim project Basic computer.circ as structural Verilog: 9 circuits, main circuit main
module main (
  input  LD_TR,
  output [6:0] out_2,
  output [15:0] out_3,
  output [15:0] out_4,
  output [2:0] out_5,
  output [15:0] out_6,
  output [6:0] out_7,
  output [15:0] out_8,
  output [2:0] out_9
);

  wire clk, CLR_PC, INC_DR, INC_PC, LD_AC, LD_AR, LD_DR, LD_IR, Memory_Read, Memory_Write;
  wire [6:0] bit_extender_1_out, bit_extender_2_out;
  wire [15:0] ALU_alu_output, Bus, Memory;

  CU cu_1 (
    .opcode(out_8[14:12]), .I(out_8[15]), .B5(out_8[5]), .DR(out_3), .CLK(clk), .LD_AR(LD_AR), .LD_AC(LD_AC),
    .CLR_PC(CLR_PC), .LD_DR(LD_DR), .LD_IR(LD_IR), .MEMORY_WRITE(Memory_Write), .MEMORY_READ(Memory_Read),
    .INC_PC(INC_PC), .INC_DR(INC_DR), .S2(out_9[2]), .S1(out_9[1]), .S0(out_9[0]), .ALU_Select_Lines(out_5));
  Bit_Extender #(.in_width(16), .out_width(7)) bit_extender_1 (.in(Bus), .out(bit_extender_1_out));
  ALU ALU (.A(out_3), .B(out_4), .Select_Lines(out_5), .ALU_Output(ALU_alu_output));
  Bit_Extender #(.in_width(16), .out_width(7)) bit_extender_2 (.in(Bus), .out(bit_extender_2_out));
  AddressRgstr AR (.Input(bit_extender_1_out), .LD(LD_AR), .CLK(clk), .Output(out_2));  // open: CLR_Signal
  WordRgstr DR (.Input(Bus), .LD(LD_DR), .CLK(clk), .INC_Signal(INC_DR), .Output(out_3));  // open: CLR_Signal
  Register #(.width(16)) register_1 (.D(ALU_alu_output), .en(LD_AC), .Q(out_4), .clk(clk));  // open: clr
  WordRgstr TR (.Input(Bus), .LD(LD_TR), .CLK(clk), .Output(out_6));  // open: CLR_Signal, INC_Signal
  Counter #(.width(7), .max('h7f)) PC (
    .D(bit_extender_2_out), .count(INC_PC), .Q(out_7), .clk(clk), .clr(CLR_PC));  // open: load, carry
  Register #(.width(16)) IR (.D(Bus), .en(LD_IR), .Q(out_8), .clk(clk));  // open: clr
  RAM #(.addrWidth(7), .dataWidth(16), .bus("separate")) ram_1 (
    .addr(out_2), .din(Bus), .data(Memory), .str(Memory_Write), .clk(clk), .ld(Memory_Read));  // open: sel, clr
  Bus_Control Bus_Control (
    .AC(out_4), .DR(out_3), .TR(out_6), .AR(out_2), .Memory(Memory), .PC(out_7), .IR(out_8),
    .Select_Lines(out_9), .Bus_Control_Output(Bus));
  Clock u_clk (.out(clk));

  // Other names for the same wires on the sheet: AC[15:0] = out_4; ALU_SELECT_LINES[2:0] = out_5; AR[6:0] = out_2;
  //   Bus_Select_Lines[2:0] = out_9; DR[15:0] = out_3; IR[15:0] = out_8; PC[6:0] = out_7; TR[15:0] = out_6
endmodule

module ALU (
  input  [15:0] A,
  input  [15:0] B,
  input  [2:0] Select_Lines,
  output [15:0] ALU_Output
);

  wire [15:0] adder_1_out, adder_2_out, and_1_out, multiplier_1_out, or_1_out, subtractor_1_out;

  Multiplier #(.width(16)) multiplier_1 (.a(A), .b(B), .out(multiplier_1_out));  // open: cin, cout
  Adder #(.width(16)) adder_1 (.a(A), .b(B), .out(adder_1_out));  // open: cin, cout
  Adder #(.width(16)) adder_2 (.a(A), .b(16'h1), .out(adder_2_out));  // open: cin, cout
  Subtractor #(.width(16)) subtractor_1 (.a(B), .b(A), .out(subtractor_1_out));  // open: bin, bout
  assign and_1_out = A & B;  // AND_Gate and_1, 16 bits wide
  assign or_1_out = A | B;  // OR_Gate or_1, 16 bits wide
  Multiplexer #(.select(3), .width(16)) multiplexer_1 (
    .in1(A), .in2(adder_1_out), .in3(subtractor_1_out), .in4(multiplier_1_out), .in5(adder_2_out),
    .in6(or_1_out), .in7(and_1_out), .out(ALU_Output), .sel(Select_Lines));  // open: in0, en
endmodule

module Bus_Control (
  input  [15:0] AC,
  input  [15:0] DR,
  input  [15:0] TR,
  input  [6:0] AR,
  input  [2:0] Select_Lines,
  input  [15:0] Memory,
  input  [6:0] PC,
  input  [15:0] IR,
  output [15:0] Bus_Control_Output
);

  wire [15:0] bit_extender_1_out, bit_extender_2_out;

  assign bit_extender_1_out = {{9{1'b0}}, AR};  // Bit_Extender bit_extender_1
  assign bit_extender_2_out = {{9{1'b0}}, PC};  // Bit_Extender bit_extender_2
  Multiplexer #(.select(3), .width(16)) multiplexer_1 (
    .in0(AC), .in1(DR), .in2(TR), .in3(bit_extender_1_out), .in4(Memory), .in5(bit_extender_2_out), .in6(IR),
    .out(Bus_Control_Output), .sel(Select_Lines));  // open: in7, en
endmodule

module WordRgstr (
  input  [15:0] Input,
  input  LD,
  input  CLK,
  input  CLR_Signal,
  input  INC_Signal,
  output [15:0] Output
);

  wire d_ff_1_q;
  wire [15:0] adder_1_out, multiplexer_1_out, multiplexer_2_out;

  Adder #(.width(16)) adder_1 (.a(Output), .b(16'h1), .out(adder_1_out));  // open: cin, cout
  Multiplexer #(.width(16)) multiplexer_1 (.in0(Output), .in1(Input), .out(multiplexer_1_out), .sel(LD));  // open: en
  Multiplexer #(.width(16)) multiplexer_2 (
    .in0(multiplexer_1_out), .in1(adder_1_out), .out(multiplexer_2_out), .sel(INC_Signal));  // open: en
  Register #(.width(16)) register_1 (.D(multiplexer_2_out), .en(1'b1), .Q(Output), .clk(CLK), .clr(d_ff_1_q));
  D_Flip_Flop d_ff_1 (.clk(CLK), .D(CLR_Signal), .Q(d_ff_1_q));  // open: Qn, preset, en, reset
endmodule

module AddressRgstr (
  input  [6:0] Input,
  input  LD,
  input  CLK,
  input  CLR_Signal,
  output [6:0] Output
);

  wire d_ff_1_q;

  Register #(.width(7)) register_1 (.D(Input), .en(LD), .Q(Output), .clk(CLK), .clr(d_ff_1_q));
  D_Flip_Flop d_ff_1 (.clk(CLK), .D(CLR_Signal), .Q(d_ff_1_q));  // open: Qn, preset, en, reset
endmodule

module CU (
  input  [2:0] opcode,
  input  I,
  input  B5,
  input  CLK,
  input  [15:0] DR,
  output LD_AR,
  output LD_AC,
  output CLR_PC,
  output LD_DR,
  output LD_IR,
  output MEMORY_WRITE,
  output MEMORY_READ,
  output INC_PC,
  output INC_DR,
  output S2,
  output S1,
  output S0,
  output [2:0] ALU_Select_Lines
);

  wire CLR_SC, d_ff_1_q, decoder_1_out0, decoder_1_out1, decoder_1_out2, decoder_1_out3, decoder_1_out4,
       decoder_1_out5, decoder_1_out6, decoder_1_out7, decoder_2_out0, decoder_2_out1, decoder_2_out2,
       decoder_2_out3, decoder_2_out4, decoder_2_out5, decoder_2_out6, I_q;
  wire [2:0] SC_q;

  D_Flip_Flop u_I (.clk(CLK), .D(I), .Q(I_q));  // open: Qn, preset, en, reset
  Decoder #(.select(3), .enable("false")) decoder_1 (
    .out0(decoder_1_out0), .out1(decoder_1_out1), .out2(decoder_1_out2), .out3(decoder_1_out3),
    .out4(decoder_1_out4), .out5(decoder_1_out5), .out6(decoder_1_out6), .out7(decoder_1_out7), .sel(opcode));
  Counter #(.width(3), .max('h7)) SC (.Q(SC_q), .clk(CLK), .clr(d_ff_1_q));  // open: load, D, count, carry
  Decoder #(.select(3), .enable("false")) decoder_2 (
    .out0(decoder_2_out0), .out1(decoder_2_out1), .out2(decoder_2_out2), .out3(decoder_2_out3),
    .out4(decoder_2_out4), .out5(decoder_2_out5), .out6(decoder_2_out6), .sel(SC_q));  // open: out7
  D_Flip_Flop d_ff_1 (.clk(CLK), .D(CLR_SC), .Q(d_ff_1_q));  // open: Qn, preset, en, reset
  Bus_Select bus_select_1 (
    .D0(decoder_1_out0), .D1(decoder_1_out1), .D2(decoder_1_out2), .D3(decoder_1_out3), .D4(decoder_1_out4),
    .D5(decoder_1_out5), .D6(decoder_1_out6), .D7(decoder_1_out7), .I(I_q), .T0(decoder_2_out0),
    .T1(decoder_2_out1), .T2(decoder_2_out2), .T3(decoder_2_out3), .T4(decoder_2_out4), .T5(decoder_2_out5),
    .T6(decoder_2_out6), .B5(B5), .S2(S2), .S1(S1), .S0(S0));
  ALU_Select alu_select_1 (
    .D0(decoder_1_out0), .D1(decoder_1_out1), .D2(decoder_1_out2), .D3(decoder_1_out3), .D4(decoder_1_out4),
    .D5(decoder_1_out5), .D6(decoder_1_out6), .D7(decoder_1_out7), .I(I_q), .T0(decoder_2_out0),
    .T1(decoder_2_out1), .T2(decoder_2_out2), .T3(decoder_2_out3), .T4(decoder_2_out4), .T5(decoder_2_out5),
    .T6(decoder_2_out6), .B5(B5), .ALU_SELECT_LINES(ALU_Select_Lines));
  CU_LogicGates cu_logicgates_1 (
    .D0(decoder_1_out0), .D1(decoder_1_out1), .D2(decoder_1_out2), .D3(decoder_1_out3), .D4(decoder_1_out4),
    .D5(decoder_1_out5), .D6(decoder_1_out6), .D7(decoder_1_out7), .I(I_q), .T0(decoder_2_out0),
    .T1(decoder_2_out1), .T2(decoder_2_out2), .T3(decoder_2_out3), .T4(decoder_2_out4), .T5(decoder_2_out5),
    .T6(decoder_2_out6), .B5(B5), .DR(DR), .LD_AR(LD_AR), .LD_AC(LD_AC), .CLR_PC(CLR_PC), .LD_DR(LD_DR),
    .LD_IR(LD_IR), .Memory_Write(MEMORY_WRITE), .Memory_Read(MEMORY_READ), .INC_PC(INC_PC), .CLR_SC(CLR_SC),
    .INC_DR(INC_DR));
endmodule

module CU_LogicGates (
  input  D0,
  input  D1,
  input  D2,
  input  D3,
  input  D4,
  input  D5,
  input  D6,
  input  D7,
  input  I,
  input  T0,
  input  T1,
  input  T2,
  input  T3,
  input  T4,
  input  T5,
  input  T6,
  input  B5,
  input  [15:0] DR,
  output LD_AR,
  output LD_AC,
  output CLR_PC,
  output LD_DR,
  output LD_IR,
  output Memory_Write,
  output Memory_Read,
  output INC_PC,
  output CLR_SC,
  output INC_DR
);

  wire and_2_out, and_3_out, and_4_out, and_5_out, and_6_out, and_8_out, and_9_out, and_10_out, and_11_out,
       and_12_out, and_13_out, and_14_out, and_15_out, and_16_out, and_17_out, and_18_out, and_19_out,
       and_20_out, and_21_out, and_22_out, and_23_out, and_24_out, and_25_out, and_26_out, and_27_out,
       and_28_out, and_29_out, and_31_out, DR_ZERO, R;

  and and_1 (R, D7, T3, ~I);  // AND_Gate
  nor nor_1 (DR_ZERO, DR[0], DR[1], DR[2], DR[3], DR[4], DR[5], DR[6], DR[7], DR[8], DR[9], DR[10], DR[11], DR[12], DR[13], DR[14], DR[15]);
  and and_2 (and_2_out, ~D7, I, T3);  // AND_Gate
  and and_3 (and_3_out, D0, T5);
  and and_4 (and_4_out, D1, T5);
  and and_5 (and_5_out, D2, T5);
  and and_6 (and_6_out, B5, R);
  and and_7 (CLR_PC, D4, T4);
  and and_8 (and_8_out, D0, T4);
  and and_9 (and_9_out, D2, T4);
  and and_10 (and_10_out, D6, T4);
  or or_1 (LD_AR, T0, and_2_out, T2);
  and and_11 (and_11_out, D1, T4);
  and and_12 (and_12_out, D6, T5);
  and and_13 (and_13_out, D3, T4);
  and and_14 (and_14_out, D5, T4);
  and and_15 (and_15_out, D6, T6);
  and and_16 (and_16_out, R, T1);
  and and_17 (and_17_out, D0, T4);
  and and_18 (and_18_out, D5, T4);
  and and_19 (and_19_out, D2, T4);
  and and_20 (and_20_out, D1, T4);
  and and_21 (and_21_out, D6, T4);
  and and_22 (and_22_out, D6, DR_ZERO, T6);
  and and_23 (and_23_out, D1, T5);
  and and_24 (and_24_out, D2, T5);
  and and_25 (and_25_out, D3, T4);
  and and_26 (and_26_out, D4, T4);
  and and_27 (and_27_out, D5, T5);
  and and_28 (and_28_out, D6, T6);
  and and_29 (and_29_out, D0, T5);
  and and_30 (INC_DR, D6, T5);
  and and_31 (and_31_out, D5, T5);
  or or_2 (LD_DR, and_8_out, and_11_out, and_9_out, and_10_out, and_12_out);
  or or_3 (Memory_Read, T1, and_17_out, and_18_out, and_19_out, and_20_out, and_21_out);
  or or_4 (INC_PC, T1, and_22_out);
  or or_5 (LD_AC, and_3_out, and_4_out, and_5_out, and_6_out, and_31_out);
  or or_6 (Memory_Write, and_13_out, and_14_out, and_15_out, and_16_out);
  or or_7 (CLR_SC, and_23_out, and_24_out, and_25_out, and_26_out, and_27_out, and_28_out, and_29_out);

  assign LD_IR = T1;
endmodule

module Bus_Select (
  input  D0,
  input  D1,
  input  D2,
  input  D3,
  input  D4,
  input  D5,
  input  D6,
  input  D7,
  input  I,
  input  T0,
  input  T1,
  input  T2,
  input  T3,
  input  T4,
  input  T5,
  input  T6,
  input  B5,
  output S2,
  output S1,
  output S0
);

  wire AC_X4, and_2_out, and_3_out, and_4_out, and_5_out, and_6_out, and_7_out, and_8_out, and_9_out,
       and_10_out, MEMORY, R;

  and and_1 (R, D7, T3, ~I);  // AND_Gate
  and and_2 (and_2_out, D3, T4);
  and and_3 (and_3_out, D5, T5);
  and and_4 (and_4_out, D0, T5);
  and and_5 (and_5_out, D6, T6);
  and and_6 (and_6_out, D0, T4);
  and and_7 (and_7_out, D5, T4);
  and and_8 (and_8_out, D2, T4);
  and and_9 (and_9_out, D1, T4);
  and and_10 (and_10_out, D6, T4);
  or or_1 (MEMORY, T1, and_6_out, and_7_out, and_8_out, and_9_out, and_10_out);
  or or_2 (AC_X4, and_2_out, and_3_out, and_4_out);
  Priority_Encoder priority_encoder_1 (
    .in0(AC_X4), .in1(and_5_out), .in2(1'b0), .in3(1'b0), .in4(MEMORY), .in5(T0), .in6(T2), .out({S2, S1, S0}));  // open: in7, en_in, gs, en_out
endmodule

module ALU_Select (
  input  D0,
  input  D1,
  input  D2,
  input  D3,
  input  D4,
  input  D5,
  input  D6,
  input  D7,
  input  I,
  input  T0,
  input  T1,
  input  T2,
  input  T3,
  input  T4,
  input  T5,
  input  T6,
  input  B5,
  output [2:0] ALU_SELECT_LINES
);

  wire R, X1, X2, X3, X4, X5;

  and and_1 (R, D7, T3, ~I);  // AND_Gate
  and and_2 (X4, D5, T5);
  and and_3 (X3, D0, T5);
  and and_4 (X2, D1, T5);
  and and_5 (X1, D2, T5);
  and and_6 (X5, R, B5);
  Priority_Encoder priority_encoder_1 (
    .in1(X1), .in2(X2), .in3(X3), .in4(X4), .in5(X5), .out(ALU_SELECT_LINES));  // open: in0, in6, in7, en_in, gs, en_out
endmodule
